# Fritzing sketch SketchEnvironment (saved by Fritzing 0.9.3b)
breadboards: 1

parts:
  Part1 = Arduino Mega ADK (Rev3)
  LCD1 = LCD screen
  PIR1 = PIR sensor
  LED1 = LED - 3mm [color="Green (555nm)" package="3 mm [THT]"]
  LED2 = LED - 3mm [color="Red (633nm)" package="3 mm [THT]"]
  LED3 = LED - 3mm [color="Blue (430nm)" package="3 mm [THT]"]
  R1 = Resistor [tolerance=±5% resistance=220 package="0805 [SMD]"]
  R2 = Resistor [tolerance=±5% resistance=220 package="0805 [SMD]"]
  R3 = Resistor [tolerance=±5% resistance=220 package="0805 [SMD]"]
  ANT1 = Antenna  # not connected
  R4 = TRIMPOT [package=trimpot_pth_s3_lock]
  Part3 = Arduino Cellular Shield

nets:
  N1: Part1.D22, LCD1.RS
  N2: Part1.D23, LCD1.E
  N3: Part1.D24, LCD1.DB4
  N4: Part1.D25, LCD1.DB5
  N5: Part1.D26, LCD1.DB6
  N6: Part1.D27, LCD1.DB7
  N7: Part1.D28, R3.Pin_1
  N8: Part1.D29, R2.Pin_1
  N9: Part1.D30, R1.Pin_1
  N10: Part1.D31, PIR1.SIG
  N11: LCD1.VSS, R4.CCW
  N12: LCD1.VDD, LCD1.V0, R4.WIPER, R4.CW
  VDD: LCD1.R/W, LCD1.LED+, PIR1.VDD, Part3.5V
  GND: LCD1.LED-, PIR1.GND, LED1.cathode, LED2.cathode, LED3.cathode, Part3.GND
  N13: LED2.anode, R2.Pin_0
  N14: LED3.anode, R3.Pin_0
